# Fritzing sketch Midterm_2 (saved by Fritzing 0.9.4)
breadboards: 1

parts:
  Argon1 = Particle Argon
  SENS1 = SoilWatch 10
  Grove1 = Grove OLED 128x96
  R1 = Resistor [tolerance=±5% resistance=220 package="2512 [SMD]"]
  R2 = Resistor [tolerance=±5% resistance=220 package="2512 [SMD]"]
  Q1 = PNP-Transistor [package="SOT-23 [SMD]"]
  Relay1 = Relay - 6 pins [package="DIP (Dual Inline) [THT]"]
  M1 = DC Motor
  Part1 = BME280 Breakout

nets:
  VCC: Argon1.3.3V, SENS1.VCC, Grove1.VCC, Relay1.VCC, Part1.3.3V
  GND: Argon1.GND, SENS1.GND, Grove1.GND, R2.Pin_0, Q1.1, Relay1.GND, Part1.GND
  N1: Argon1.MO, R2.Pin_1, Q1.0
  N2: Argon1.SDA, Grove1.SDA, Part1.SDI/SDA
  N3: Argon1.SCL, Grove1.SCL
  N4: Argon1.VUSB, R1.Pin_1, Relay1.ON
  N5: R1.Pin_0, Q1.2, Relay1.IN
  N6: Relay1.COM, M1.pin_1

custom parts:
  Particle Argon: The Argon is a powerful Wi-Fi enabled development board that can act as either a standalone Wi-Fi endpoint or Wi-Fi enabled gateway for Particle Mesh networks. It is based on the Nordic nRF52840 and has built-in battery charging circuitry so it’s easy to connect a Li-Po and deploy your local network in minutes. The Argon is great for connecting existing projects to the Particle Device Cloud or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
  SoilWatch 10: SoilWatch 10 - Capacitive soil moisture sensor
  Relay - 6 pins: A DIP stand-in part for whatever IC you want. With 6 pins on a 900mil dual inline package (DIP) footprint.
